// Logisim project processor.circ as structural Verilog: 1 circuit, main circuit main
module main (
);

  // regfile regfile_1: pin names not known
  // alu alu_1: pin names not known
endmodule
